// Digital circuit conway_ttl.dig as structural Verilog
module conway_ttl (
  input  in_1,
  input  in_2,
  input  in_3,
  input  in_4,
  input  in_5,
  input  in_6,
  input  in_7,
  input  in_8,
  input  in_9
);

  wire _74250_1_p10, _74250_1_p22, _74250_1_p23, _74250_1_p24, _74283_1_pin1, _74283_1_pin4, _74283_1_pin9,
       _74283_1_pin10, _74283_2_pin10;

  // _74250 _74250_1: pin names not known; wires that end beside it: 1'b0, 1'b0, 1'b0, 1'b0, 1'b1, in_9, 1'b0, 1'b0, 1'b0, _74250_1_p10, in_7, 1'b0, 1'b1, 1'b0, in_9, 1'b1, 1'b0, 1'b0, 1'b0, 1'b0, 1'b0, _74250_1_p22, _74250_1_p23, _74250_1_p24
  _74283 _74283_1 (
    .pin1(_74283_1_pin1), .pin2(1'b0), .pin3(1'b0), .pin4(_74283_1_pin4), .pin5(in_3), .pin6(in_2),
    .pin7(in_1), .pin8(1'b0), .pin9(_74283_1_pin9), .pin10(_74283_1_pin10), .pin11(in_6), .pin12(in_5),
    .pin14(in_4), .pin15(1'b1), .pin16(1'b1));  // open: pin13
  _74283 _74283_2 (
    .pin1(_74250_1_p23), .pin2(_74283_1_pin9), .pin3(_74283_1_pin1), .pin4(_74250_1_p22),
    .pin5(_74283_1_pin4), .pin6(_74283_1_pin10), .pin7(in_8), .pin8(1'b0), .pin10(_74283_2_pin10),
    .pin11(_74250_1_p10), .pin12(1'b1), .pin13(_74250_1_p24), .pin14(1'b0), .pin15(1'b0), .pin16(1'b1));  // open: pin9
  LED led_1 (.in(_74283_2_pin10));

  // Notes on the sheet:
  //   Old state
  //   Neighbor cells states
  //   New state
endmodule
