// Digital circuit conway_ttl_only_adders.dig as structural Verilog
module conway_ttl_only_adders (
  input  in_1,
  input  in_2,
  input  in_3,
  input  in_4,
  input  in_5,
  input  in_6,
  input  in_7,
  input  in_8,
  input  in_9
);

  wire _74283_1_pin2, _74283_1_pin7, _74283_1_pin11, _74283_1_pin12, _74283_1_pin13, _74283_2_pin3,
       _74283_2_pin6, _74283_2_pin15, _74283_3_pin1, _74283_3_pin4, _74283_3_pin9, _74283_3_pin10;

  _74283 _74283_1 (
    .pin2(_74283_1_pin2), .pin3(1'b0), .pin5(1'b1), .pin6(in_9), .pin7(_74283_1_pin7), .pin8(1'b0),
    .pin9(_74283_1_pin2), .pin11(_74283_1_pin11), .pin12(_74283_1_pin12), .pin13(_74283_1_pin13),
    .pin14(1'b0), .pin15(1'b0), .pin16(1'b1));  // open: pin1, pin4, pin10
  _74283 _74283_2 (
    .pin1(_74283_1_pin12), .pin2(1'b0), .pin3(_74283_2_pin3), .pin4(_74283_1_pin7), .pin5(in_7),
    .pin6(_74283_2_pin6), .pin7(1'b0), .pin8(1'b0), .pin10(_74283_1_pin11), .pin11(1'b0), .pin12(1'b1),
    .pin14(1'b1), .pin15(_74283_2_pin15), .pin16(1'b1));  // open: pin9, pin13
  _74283 _74283_3 (
    .pin1(_74283_3_pin1), .pin2(1'b0), .pin3(1'b0), .pin4(_74283_3_pin4), .pin5(in_3), .pin6(in_2),
    .pin7(in_1), .pin8(1'b0), .pin9(_74283_3_pin9), .pin10(_74283_3_pin10), .pin11(in_6), .pin12(in_5),
    .pin14(in_4), .pin15(1'b1), .pin16(1'b1));  // open: pin13
  _74283 _74283_4 (
    .pin1(_74283_2_pin3), .pin2(_74283_3_pin9), .pin3(_74283_3_pin1), .pin4(_74283_2_pin6),
    .pin5(_74283_3_pin4), .pin6(_74283_3_pin10), .pin7(in_8), .pin8(1'b0), .pin11(1'b1), .pin12(1'b1),
    .pin13(_74283_2_pin15), .pin14(1'b0), .pin15(1'b0), .pin16(1'b1));  // open: pin9, pin10
  LED led_1 (.in(_74283_1_pin13));

  // Notes on the sheet:
  //   Old state
  //   Neighbor cells states
  //   New state
endmodule
